# Fritzing sketch Gas_Sensor_Flame_Sensor_Buzzer (saved by Fritzing 0.9.3b)
breadboards: 1

parts:
  부품1 = Arduino Uno (Rev3)
  LED1 = LED - 5mm [color="Red (633nm)" package="5 mm [THT]"]
  LED2 = LED - 5mm [color="Red (633nm)" package="5 mm [THT]"]
  R1 = Resistor [tolerance=±5% resistance=220 package=THT]
  R2 = Resistor [tolerance=±5% resistance=220 package=THT]
  R3 = Resistor [tolerance=±5% resistance=220 package=THT]
  J1 = Piezo Speaker
  U2 = GAS_SENSOR [package=mq-3]
  부품2 = IMU Analog Combo Board - 5 Degrees of Freedom

nets:
  N1: 부품1.A4/SDA, 부품2.Y4.5OUT
  N2: 부품1.A5/SCL, U2.A1
  N3: 부품1.D10_PWM/SS, J1.pin1
  N4: 부품1.D11_PWM/MOSI, LED2.cathode
  N5: 부품1.D12/MISO, LED1.cathode
  N6: 부품1.GND, U2.B1, 부품2.X4.5OUT
  N7: LED1.anode, R1.Pin_0
  N8: LED2.anode, R2.Pin_0
  N9: R1.Pin_1, R2.Pin_1, R3.Pin_1
  N10: R3.Pin_0, J1.pin2
