# Fritzing sketch AR01_4led (saved by Fritzing 0.9.3b)
breadboards: 1

parts:
  부품1 = Arduino Uno (Rev3)
  R1 = Resistor [tolerance=±5% resistance=220 package=THT]
  R2 = Resistor [tolerance=±5% resistance=220 package=THT]
  R4 = Resistor [tolerance=±5% resistance=220 package=THT]
  LED1 = LED - 5mm [color="Red (633nm)" package="5 mm [THT]"]
  LED2 = LED - 5mm [color="Red (633nm)" package="5 mm [THT]"]
  LED3 = LED - 5mm [color="Red (633nm)" package="5 mm [THT]"]
  R5 = Resistor [tolerance=±5% resistance=220 package=THT]
  LED4 = LED - 5mm [color="Red (633nm)" package="5 mm [THT]"]

nets:
  N1: 부품1.D9_PWM, LED1.cathode
  N2: 부품1.D3_PWM, LED4.cathode
  N3: 부품1.D5_PWM, LED3.cathode
  N4: 부품1.D6_PWM, LED2.cathode
  N5: R1.Pin_0, LED1.anode
  N6: R1.Pin_1, R4.Pin_1, R5.Pin_1
  N7: R2.Pin_0, LED2.anode
  N8: R4.Pin_0, LED4.anode
  N9: LED3.anode, R5.Pin_0
